// Logisim project Brookshear.circ as structural Verilog
module main (
);

  wire demultiplexer_1_out0, demultiplexer_1_out1, demultiplexer_1_out2, demultiplexer_1_out3,
       demultiplexer_1_out4, demultiplexer_1_out5, demultiplexer_1_out6, demultiplexer_1_out7,
       demultiplexer_1_out8, demultiplexer_1_out9, demultiplexer_1_out10, demultiplexer_1_out11,
       demultiplexer_1_out12, demultiplexer_1_out13, demultiplexer_1_out14, demultiplexer_1_out15, undriven_2;
  wire [7:0] controlled_buffer_1_out, register_1_q, register_2_q, register_3_q, register_4_q, register_5_q,
       register_6_q, register_7_q, register_8_q, register_9_q, register_10_q, register_11_q, register_12_q,
       register_13_q, register_14_q, register_15_q, register_16_q, undriven;

  Demultiplexer #(.select(4)) demultiplexer_1 (
    .out0(demultiplexer_1_out0), .out1(demultiplexer_1_out1), .out2(demultiplexer_1_out2),
    .out3(demultiplexer_1_out3), .out4(demultiplexer_1_out4), .out5(demultiplexer_1_out5),
    .out6(demultiplexer_1_out6), .out7(demultiplexer_1_out7), .out8(demultiplexer_1_out8),
    .out9(demultiplexer_1_out9), .out10(demultiplexer_1_out10), .out11(demultiplexer_1_out11),
    .out12(demultiplexer_1_out12), .out13(demultiplexer_1_out13), .out14(demultiplexer_1_out14),
    .out15(demultiplexer_1_out15));  // open: in, sel
  Register register_1 (.D(undriven), .en(demultiplexer_1_out15), .clk(undriven_2), .Q(register_1_q));  // open: clr
  Register register_2 (.D(undriven), .en(demultiplexer_1_out14), .clk(undriven_2), .Q(register_2_q));  // open: clr
  Register register_3 (.D(undriven), .en(demultiplexer_1_out13), .clk(undriven_2), .Q(register_3_q));  // open: clr
  Register register_4 (.D(undriven), .en(demultiplexer_1_out12), .clk(undriven_2), .Q(register_4_q));  // open: clr
  Register register_5 (.D(undriven), .en(demultiplexer_1_out11), .clk(undriven_2), .Q(register_5_q));  // open: clr
  Register register_6 (.D(undriven), .en(demultiplexer_1_out10), .clk(undriven_2), .Q(register_6_q));  // open: clr
  Register register_7 (.D(undriven), .en(demultiplexer_1_out9), .clk(undriven_2), .Q(register_7_q));  // open: clr
  Register register_8 (.D(undriven), .en(demultiplexer_1_out8), .clk(undriven_2), .Q(register_8_q));  // open: clr
  Register register_9 (.D(undriven), .en(demultiplexer_1_out7), .clk(undriven_2), .Q(register_9_q));  // open: clr
  Register register_10 (.D(undriven), .en(demultiplexer_1_out6), .clk(undriven_2), .Q(register_10_q));  // open: clr
  Register register_11 (.D(undriven), .en(demultiplexer_1_out5), .clk(undriven_2), .Q(register_11_q));  // open: clr
  Register register_12 (.D(undriven), .en(demultiplexer_1_out4), .clk(undriven_2), .Q(register_12_q));  // open: clr
  Register register_13 (.D(undriven), .en(demultiplexer_1_out3), .clk(undriven_2), .Q(register_13_q));  // open: clr
  Register register_14 (.D(undriven), .en(demultiplexer_1_out2), .clk(undriven_2), .Q(register_14_q));  // open: clr
  Register register_15 (.D(undriven), .en(demultiplexer_1_out1), .clk(undriven_2), .Q(register_15_q));  // open: clr
  Register register_16 (.D(undriven), .en(demultiplexer_1_out0), .clk(undriven_2), .Q(register_16_q));  // open: clr
  ALU alu_1 ();
  Controlled_Buffer #(.width(8)) controlled_buffer_1 (.in(register_1_q), .out(controlled_buffer_1_out));  // open: en
  Controlled_Buffer #(.width(8)) controlled_buffer_2 (.in(register_2_q), .out(controlled_buffer_1_out));  // open: en
  Controlled_Buffer #(.width(8)) controlled_buffer_3 (.in(register_3_q), .out(controlled_buffer_1_out));  // open: en
  Controlled_Buffer #(.width(8)) controlled_buffer_4 (.in(register_4_q), .out(controlled_buffer_1_out));  // open: en
  Controlled_Buffer #(.width(8)) controlled_buffer_5 (.in(register_5_q), .out(controlled_buffer_1_out));  // open: en
  Controlled_Buffer #(.width(8)) controlled_buffer_6 (.in(register_6_q), .out(controlled_buffer_1_out));  // open: en
  Controlled_Buffer #(.width(8)) controlled_buffer_7 (.in(register_7_q), .out(controlled_buffer_1_out));  // open: en
  Controlled_Buffer #(.width(8)) controlled_buffer_8 (.in(register_8_q), .out(controlled_buffer_1_out));  // open: en
  Controlled_Buffer #(.width(8)) controlled_buffer_9 (.in(register_9_q), .out(controlled_buffer_1_out));  // open: en
  Controlled_Buffer #(.width(8)) controlled_buffer_10 (.in(register_10_q), .out(controlled_buffer_1_out));  // open: en
  Controlled_Buffer #(.width(8)) controlled_buffer_11 (.in(register_11_q), .out(controlled_buffer_1_out));  // open: en
  Controlled_Buffer #(.width(8)) controlled_buffer_12 (.in(register_12_q), .out(controlled_buffer_1_out));  // open: en
  Controlled_Buffer #(.width(8)) controlled_buffer_13 (.in(register_13_q), .out(controlled_buffer_1_out));  // open: en
  Controlled_Buffer #(.width(8)) controlled_buffer_14 (.in(register_14_q), .out(controlled_buffer_1_out));  // open: en
  Controlled_Buffer #(.width(8)) controlled_buffer_15 (.in(register_15_q), .out(controlled_buffer_1_out));  // open: en
  Controlled_Buffer #(.width(8)) controlled_buffer_16 (.in(register_16_q), .out(controlled_buffer_1_out));  // open: en
  CIR cir_1 ();
  PC pc_1 ();
  MainMemory mainmemory_1 ();  // open: CLK, READ, WRITE, DATA_IN, READ_ADDRESS, WRITE_ADDRESS, DATA_OUT

  // Notes on the sheet:
  //   Register Select
  //   Registers
  //   Register Bus
endmodule

module MainMemory (
  input  CLK,
  input  READ,
  input  WRITE,
  input  [7:0] DATA_IN,
  input  [7:0] READ_ADDRESS,
  input  [7:0] WRITE_ADDRESS,
  output [7:0] DATA_OUT
);

  wire and_1_out, and_2_out, and_3_out, and_4_out, and_5_out, and_6_out, and_7_out, and_8_out, and_9_out,
       and_10_out, and_11_out, and_12_out, and_13_out, and_14_out, and_15_out, and_16_out, undriven,
       undriven_2, undriven_3, undriven_4, undriven_5, undriven_6, undriven_7, undriven_8, undriven_9,
       undriven_10, undriven_11, undriven_12, undriven_13, undriven_14, undriven_15, undriven_16,
       undriven_17, undriven_18, undriven_19, undriven_20, undriven_21, undriven_22, undriven_23,
       undriven_24, undriven_25, undriven_26, undriven_27, undriven_28, undriven_29, undriven_30,
       undriven_31, undriven_32, undriven_33, undriven_34, undriven_35, undriven_36, undriven_37,
       undriven_38, undriven_39, undriven_40;
  wire [7:0] register_1_q, register_2_q, register_3_q, register_4_q, register_5_q, register_6_q,
       register_7_q, register_8_q, register_9_q, register_10_q, register_11_q, register_12_q, register_13_q,
       register_14_q, register_15_q, register_16_q;

  Demultiplexer #(.select(4)) demultiplexer_1 ();  // open: out0, out1, out2, out3, out4, out5, out6, out7, out8, out9, out10, out11, out12, out13, out14, out15, in, sel
  Demultiplexer #(.select(4)) demultiplexer_2 ();  // open: out0, out1, out2, out3, out4, out5, out6, out7, out8, out9, out10, out11, out12, out13, out14, out15, in, sel
  Register register_1 (.D(DATA_IN), .en(undriven), .clk(CLK), .Q(register_1_q));  // open: clr
  Register register_2 (.D(DATA_IN), .en(undriven_2), .clk(CLK), .Q(register_2_q));  // open: clr
  Register register_3 (.D(DATA_IN), .en(undriven_3), .clk(undriven_17), .Q(register_3_q));  // open: clr
  Register register_4 (.D(DATA_IN), .en(undriven_4), .clk(undriven_17), .Q(register_4_q));  // open: clr
  Register register_5 (.D(DATA_IN), .en(undriven_5), .clk(undriven_18), .Q(register_5_q));  // open: clr
  Register register_6 (.D(DATA_IN), .en(undriven_6), .clk(undriven_18), .Q(register_6_q));  // open: clr
  Register register_7 (.D(DATA_IN), .en(undriven_7), .clk(undriven_19), .Q(register_7_q));  // open: clr
  Register register_8 (.D(DATA_IN), .en(undriven_8), .clk(undriven_19), .Q(register_8_q));  // open: clr
  Register register_9 (.D(DATA_IN), .en(undriven_9), .clk(undriven_20), .Q(register_9_q));  // open: clr
  Register register_10 (.D(DATA_IN), .en(undriven_10), .clk(undriven_20), .Q(register_10_q));  // open: clr
  Register register_11 (.D(DATA_IN), .en(undriven_11), .clk(undriven_21), .Q(register_11_q));  // open: clr
  Register register_12 (.D(DATA_IN), .en(undriven_12), .clk(undriven_21), .Q(register_12_q));  // open: clr
  Register register_13 (.D(DATA_IN), .en(undriven_13), .clk(undriven_22), .Q(register_13_q));  // open: clr
  Register register_14 (.D(DATA_IN), .en(undriven_14), .clk(undriven_22), .Q(register_14_q));  // open: clr
  Register register_15 (.D(DATA_IN), .en(undriven_15), .clk(undriven_23), .Q(register_15_q));  // open: clr
  Register register_16 (.D(DATA_IN), .en(undriven_16), .clk(undriven_23), .Q(register_16_q));  // open: clr
  and and_1 (and_1_out, undriven_24, undriven_40);
  assign DATA_OUT = and_1_out ? register_1_q : 8'bz;  // Controlled_Buffer controlled_buffer_1
  and and_2 (and_2_out, undriven_25, undriven_40);
  assign DATA_OUT = and_2_out ? register_2_q : 8'bz;  // Controlled_Buffer controlled_buffer_2
  and and_3 (and_3_out, undriven_26, undriven_40);
  assign DATA_OUT = and_3_out ? register_3_q : 8'bz;  // Controlled_Buffer controlled_buffer_3
  and and_4 (and_4_out, undriven_27, undriven_40);
  assign DATA_OUT = and_4_out ? register_4_q : 8'bz;  // Controlled_Buffer controlled_buffer_4
  and and_5 (and_5_out, undriven_28, undriven_40);
  assign DATA_OUT = and_5_out ? register_5_q : 8'bz;  // Controlled_Buffer controlled_buffer_5
  and and_6 (and_6_out, undriven_29, undriven_40);
  assign DATA_OUT = and_6_out ? register_6_q : 8'bz;  // Controlled_Buffer controlled_buffer_6
  and and_7 (and_7_out, undriven_30, undriven_40);
  assign DATA_OUT = and_7_out ? register_7_q : 8'bz;  // Controlled_Buffer controlled_buffer_7
  and and_8 (and_8_out, undriven_31, undriven_40);
  assign DATA_OUT = and_8_out ? register_8_q : 8'bz;  // Controlled_Buffer controlled_buffer_8
  and and_9 (and_9_out, undriven_32, undriven_40);
  assign DATA_OUT = and_9_out ? register_9_q : 8'bz;  // Controlled_Buffer controlled_buffer_9
  and and_10 (and_10_out, undriven_33, undriven_40);
  assign DATA_OUT = and_10_out ? register_10_q : 8'bz;  // Controlled_Buffer controlled_buffer_10
  and and_11 (and_11_out, undriven_34, undriven_40);
  assign DATA_OUT = and_11_out ? register_11_q : 8'bz;  // Controlled_Buffer controlled_buffer_11
  and and_12 (and_12_out, undriven_35, undriven_40);
  assign DATA_OUT = and_12_out ? register_12_q : 8'bz;  // Controlled_Buffer controlled_buffer_12
  and and_13 (and_13_out, undriven_36, undriven_40);
  assign DATA_OUT = and_13_out ? register_13_q : 8'bz;  // Controlled_Buffer controlled_buffer_13
  and and_14 (and_14_out, undriven_37, undriven_40);
  assign DATA_OUT = and_14_out ? register_14_q : 8'bz;  // Controlled_Buffer controlled_buffer_14
  and and_15 (and_15_out, undriven_38, undriven_40);
  assign DATA_OUT = and_15_out ? register_15_q : 8'bz;  // Controlled_Buffer controlled_buffer_15
  and and_16 (and_16_out, undriven_39, undriven_40);
  assign DATA_OUT = and_16_out ? register_16_q : 8'bz;  // Controlled_Buffer controlled_buffer_16
  Demultiplexer #(.select(4)) demultiplexer_3 ();  // open: out0, out1, out2, out3, out4, out5, out6, out7, out8, out9, out10, out11, out12, out13, out14, out15, in, sel
  Demultiplexer #(.select(4)) demultiplexer_4 ();  // open: out0, out1, out2, out3, out4, out5, out6, out7, out8, out9, out10, out11, out12, out13, out14, out15, in, sel
endmodule
